# Fritzing sketch Würfel 8x8 DOT Matrix RGB LED (saved by Fritzing 1.0.6)
breadboards: 1

parts:
  U1 = WS2812 RGB LED matrix 8x8
  Bauteil1 = Arduino Uno (Rev3)
  S1 = Pushbutton [package="[THT]"]
  J1 = Piezo Speaker

nets (from the breadboard view):
  GND: U1.GND, Bauteil1.GND, Bauteil1.D2, S1.Pin_1, S1.Pin_2, J1.pin1
  VCC: U1.VCC, Bauteil1.5V
  N1: U1.DIN, Bauteil1.D6_PWM
  N2: Bauteil1.D9_PWM, J1.pin2
  N3: S1.Pin_3, S1.Pin_4

custom parts:
  WS2812 RGB LED matrix 8x8: WS2812 matrix 8x8
